// Logisim project Gusita_Claudiu_Calculator_de_buzunar.circ as structural Verilog
module main (
  input  [7:0] Input_bus_1,
  input  [7:0] Input_bus_2,
  input  [1:0] Input_bus_3,
  output Output_1,
  output [6:0] Output_bus_1,
  output Output_2,
  output Output_3,
  output [3:0] Output_bus_2
);

  wire clock_1_out;
  wire [1:0] counter_1_output;
  wire [3:0] mux_ssd_1_rez;
  wire [15:0] impartitor_1_rez, inmultitor_1_prod, mux_1_rezultat, scazator_8_biti_1_d, sumator_1_s;

  sumator sumator_1 (.a(Input_bus_1), .b(Input_bus_2), .s(sumator_1_s), .cout(Output_1));
  scazator_8_biti scazator_8_biti_1 (.a(Input_bus_1), .b(Input_bus_2), .d(scazator_8_biti_1_d), .bout(Output_2));
  inmultitor inmultitor_1 (.a(Input_bus_1), .b(Input_bus_2), .prod(inmultitor_1_prod));
  impartitor impartitor_1 (.a(Input_bus_1), .b(Input_bus_2), .rez(impartitor_1_rez), .eroare(Output_3));
  Clock clock_1 (.out(clock_1_out));
  mux mux_1 (
    .suma(sumator_1_s), .diferenta(scazator_8_biti_1_d), .inmultire(inmultitor_1_prod),
    .impartire(impartitor_1_rez), .semn(Input_bus_3), .rezultat(mux_1_rezultat));
  counter counter_1 (.clock(clock_1_out), .\output (counter_1_output));
  mux_SSD mux_ssd_1 (
    .digit1(mux_1_rezultat[3:0]), .digit2(mux_1_rezultat[7:4]), .digit3(mux_1_rezultat[11:8]),
    .digit4(mux_1_rezultat[15:12]), .sel1(counter_1_output[0]), .sel2(counter_1_output[1]),
    .rez(mux_ssd_1_rez));
  BCD_7_segmente bcd_7_segmente_1 (.i(mux_ssd_1_rez), .o(Output_bus_1));
  mux_SSD mux_ssd_2 (
    .digit1(4'b0001), .digit2(4'b0010), .digit3(4'b0100), .digit4(4'b1000), .sel1(counter_1_output[0]),
    .sel2(counter_1_output[1]), .rez(Output_bus_2));
endmodule

// VHDL entity CALCULATOR_DE_BUZUNAR, as the project stores it:
--------------------------------------------------------------------------------
-- Project :
-- File    :
-- Autor   :
-- Date    :
--
--------------------------------------------------------------------------------
-- Description :
--
--------------------------------------------------------------------------------

LIBRARY ieee;
USE ieee.std_logic_1164.all;

ENTITY CALCULATOR_DE_BUZUNAR IS
  PORT (
  ------------------------------------------------------------------------------
  --Insert input ports below
    clock      : IN  std_logic;                    -- input bit example
    val        : IN  std_logic_vector(3 DOWNTO 0); -- input vector example
  ------------------------------------------------------------------------------
  --Insert output ports below
    max        : OUT std_logic;                    -- output bit example
    cpt        : OUT std_logic_vector(3 DOWNTO 0)  -- output vector example
    );
END CALCULATOR_DE_BUZUNAR;

--------------------------------------------------------------------------------
--Complete your VHDL description below
--------------------------------------------------------------------------------

ARCHITECTURE TypeArchitecture OF CALCULATOR_DE_BUZUNAR IS

BEGIN


END TypeArchitecture;

// VHDL entity sumator, as the project stores it:
--------------------------------------------------------------------------------
-- Project :
-- File    :
-- Autor   :
-- Date    :
--
--------------------------------------------------------------------------------
-- Description :
--
--------------------------------------------------------------------------------

LIBRARY ieee;
USE ieee.std_logic_1164.all;

ENTITY sumator IS
  PORT(
		a: in std_logic_vector(7 downto 0);
		b: in std_logic_vector(7 downto 0);
  		s:out std_logic_vector(15 downto 0);
  		cout:out std_logic);
END sumator;
--------------------------------------------------------------------------------
--Complete your VHDL description below
--------------------------------------------------------------------------------

ARCHITECTURE structural OF sumator IS

component sumator1 is
port( a,b,cin:in std_logic;
	 s:out std_logic;
	 cout: out std_logic);
end component;

signal c2, c3, c4, c5, c6, c7, c8 : std_logic;
BEGIN
s(15 downto 8)<="00000000";
suma1: sumator1 port map(a(0), b(0), '0', s(0), c2);
suma2: sumator1 port map(a(1), b(1), c2, s(1), c3);
suma3: sumator1 port map(a(2), b(2), c3, s(2), c4);
suma4: sumator1 port map(a(3), b(3), c4, s(3), c5);
suma5: sumator1 port map(a(4), b(4), c5, s(4), c6);
suma6: sumator1 port map(a(5), b(5), c6, s(5), c7);
suma7: sumator1 port map(a(6), b(6), c7, s(6), c8);
suma8: sumator1 port map(a(7), b(7), c8, s(7), cout);
end structural;

LIBRARY ieee;
USE ieee.std_logic_1164.all;

entity sumator1 is
port( a,b,cin: in std_logic;
		s:out std_logic;
		cout: out std_logic);
end sumator1;
architecture flux_de_date of sumator1 is

signal inter:std_logic;
BEGIN
inter<=a xor b after 1 ns;
s <= inter xor cin after 1 ns;
cout<= (a and b) or (inter and cin) after 2 ns;
end flux_de_date;

// VHDL entity scazator_8_biti, as the project stores it:
--------------------------------------------------------------------------------
-- Project :
-- File    :
-- Autor   :
-- Date    :
--
--------------------------------------------------------------------------------
-- Description :
--
--------------------------------------------------------------------------------

LIBRARY ieee;
USE ieee.std_logic_1164.all;

ENTITY scazator_8_biti IS
  PORT (
 		 a : in std_logic_vector(7 downto 0);
  		 b : in std_logic_vector(7 downto 0);
  		 d : out std_logic_vector(15 downto 0);
  		 bout : out std_logic);
END scazator_8_biti;


--------------------------------------------------------------------------------
--Complete your VHDL description below
--------------------------------------------------------------------------------

ARCHITECTURE strucutural OF scazator_8_biti IS
component scazator_1_bit is
  PORT (
  		a:in std_logic;
  		b:in std_logic;
  		bin:in std_logic;
  		d:out std_logic;
  		bout:out std_logic
    );
end component;
signal c2,c3,c4,c5,c6,c7,c8:std_logic;
BEGIN
d(15 downto 8)<="00000000";
dif1:scazator_1_bit port map(a(0),b(0),'0',d(0),c2);

dif2:scazator_1_bit port map(a(1),b(1),c2,d(1),c3);

dif3:scazator_1_bit port map(a(2),b(2),c3,d(2),c4);

dif4:scazator_1_bit port map(a(3),b(3),c4,d(3),c5);

dif5:scazator_1_bit port map(a(4),b(4),c5,d(4),c6);

dif6:scazator_1_bit port map(a(5),b(5),c6,d(5),c7);

dif7:scazator_1_bit port map(a(6),b(6),c7,d(6),c8);

dif8:scazator_1_bit port map(a(7),b(7),c8,d(7),bout);

END strucutural;

LIBRARY ieee;
USE ieee.std_logic_1164.all;
ENTITY scazator_1_bit IS
  PORT (
  		a:in std_logic;
  		b:in std_logic;
  		bin:in std_logic;
  		d:out std_logic;
  		bout:out std_logic
    );
END scazator_1_bit;

ARCHITECTURE flux_de_date OF scazator_1_bit IS
BEGIN
d<=(a xor b)xor bin;
bout<=(((not a) and b)or((not a)and bin))or(b and bin);
END flux_de_date;

// VHDL entity inmultitor, as the project stores it:
--------------------------------------------------------------------------------
-- Project :
-- File    :
-- Autor   :
-- Date    :
--
--------------------------------------------------------------------------------
-- Description :
--
--------------------------------------------------------------------------------

LIBRARY ieee;
USE ieee.std_logic_1164.all;
use ieee.numeric_std.all;
use ieee.std_logic_unsigned.all;
use ieee.std_logic_arith.all;
ENTITY inmultitor IS
  PORT (
  		a:in std_logic_vector(7 downto 0);
  		b:in std_logic_vector(7 downto 0);
  		prod:out std_logic_vector(15 downto 0)
  );
END inmultitor;

--------------------------------------------------------------------------------
--Complete your VHDL description below
--------------------------------------------------------------------------------

ARCHITECTURE comportamentala OF inmultitor IS
signal n: integer;
begin
n<=conv_integer(b);
process(a,n)
variable aux:std_logic_vector(15 downto 0);
variable aux_b:integer;
begin
aux:="0000000000000000";
aux_b:=1;
eticheta:for k in 256 downto 1 loop
if aux_b<=n then
aux:=aux+a;
end if;
aux_b:=aux_b+1;
end loop;
if n=0 then aux:="0000000000000000";
end if;
prod<=aux;
end process;
END comportamentala;

// VHDL entity impartitor, as the project stores it:
--------------------------------------------------------------------------------
-- Project :
-- File    :
-- Autor   :
-- Date    :
--
--------------------------------------------------------------------------------
-- Description :
--
--------------------------------------------------------------------------------

LIBRARY ieee;
USE ieee.std_logic_1164.all;
use ieee.numeric_std.all;
use ieee.std_logic_unsigned.all;
use ieee.std_logic_arith.all;
ENTITY impartitor IS
  PORT (
		a:in std_logic_vector(7 downto 0);
		b:in std_logic_vector(7 downto 0);
		rez:out std_logic_vector(15 downto 0);
		eroare:out std_logic
    );
END impartitor;

--------------------------------------------------------------------------------
--Complete your VHDL description below
--------------------------------------------------------------------------------

ARCHITECTURE comportamental OF impartitor IS
signal aux_eroare:std_logic;
signal n:integer;
BEGIN
n<=conv_integer(b);
process(a,b,aux_eroare)
variable aux_rest:std_logic_vector(7 downto 0);
variable aux_cat:std_logic_vector(7 downto 0);
variable aux_a:std_logic_vector(7 downto 0);
variable ok:std_logic;
begin
aux_cat:="00000000";
aux_a:=a;
aux_eroare<='0';

if a<b then aux_rest:=a;
aux_cat:="00000000";

else
eticheta: for k in 255 downto 0 loop
if aux_a>=b then aux_a:=aux_a-b;
aux_cat:=aux_cat+1;
end if;
end loop;
aux_rest:=aux_a;
end if;
if b="00000000"then aux_eroare<='1';

aux_rest:="00000000";
aux_cat:="00000000";

end if;

rez<=aux_cat&aux_rest;
eroare<=aux_eroare;

end process;
END comportamental;

// VHDL entity mux, as the project stores it:
--------------------------------------------------------------------------------
-- Project :
-- File    :
-- Autor   :
-- Date    :
--
--------------------------------------------------------------------------------
-- Description :
--
--------------------------------------------------------------------------------

LIBRARY ieee;
USE ieee.std_logic_1164.all;

ENTITY mux IS
  PORT (
		suma:in std_logic_vector(15 downto 0);
		diferenta:in std_logic_vector(15 downto 0);
		inmultire: in std_logic_vector(15 downto 0);
		impartire:in std_logic_vector(15 downto 0);
		semn:in std_logic_vector(1 downto 0);
		rezultat:out std_logic_vector(15 downto 0)
    );
END mux;

--------------------------------------------------------------------------------
--Complete your VHDL description below
--------------------------------------------------------------------------------

ARCHITECTURE TypeArchitecture OF mux IS
signal aux:std_logic_vector(15 downto 0);
BEGIN
process(semn,suma,diferenta,inmultire,impartire)
begin
case(semn) is 
when "00"=>aux<=suma;
when "01"=>aux<=diferenta;
when "10"=>aux<=inmultire;
when others=>aux<=impartire;
end case;
end process;
rezultat<=aux;
END TypeArchitecture;

// VHDL entity divizor_de_frecventa, as the project stores it:
--------------------------------------------------------------------------------
-- Project :
-- File    :
-- Autor   :
-- Date    :
--
--------------------------------------------------------------------------------
-- Description :
--
--------------------------------------------------------------------------------

LIBRARY ieee;
USE ieee.std_logic_1164.all;
use ieee.std_logic_unsigned.all;
ENTITY divizor_de_frecventa IS
  PORT (
  		clock:in std_logic;
  		div_clk: out std_logic
    );
END divizor_de_frecventa;

ARCHITECTURE TypeArchitecture OF divizor_de_frecventa IS
signal tmp: std_logic_vector(6 downto 0):=(others =>'0');
BEGIN
process(clock)
begin
	if(rising_edge(clock))then 
		if tmp=("1100011")then tmp<="0000000";
			elsif(tmp<="0110001")then 
							tmp<=tmp+1;
							div_clk<='0';
			else div_clk<='1';
			tmp<=tmp+1;
	end if;
	end if;
end process;

END TypeArchitecture;

// VHDL entity counter, as the project stores it:
--------------------------------------------------------------------------------
-- Project :
-- File    :
-- Autor   :
-- Date    :
--
--------------------------------------------------------------------------------
-- Description :
--
--------------------------------------------------------------------------------

LIBRARY ieee;
USE ieee.std_logic_1164.all;

use ieee.std_logic_unsigned.all;
ENTITY counter IS
  PORT (
  		clock:in std_logic;
  		output:out std_logic_vector(1 downto 0)
    );
END counter;

--------------------------------------------------------------------------------
--Complete your VHDL description below
--------------------------------------------------------------------------------

ARCHITECTURE TypeArchitecture OF counter IS

BEGIN
process(clock)
variable aux:std_logic_vector(16 downto 0):="00000000000000000";

begin
if(clock'event and clock='1')then
aux:=aux+1;
end if;
output(1)<=aux(16);
output(0)<=aux(15);
end process;
END TypeArchitecture;

// VHDL entity mux_SSD, as the project stores it:
--------------------------------------------------------------------------------
-- Project :
-- File    :
-- Autor   :
-- Date    :
--
--------------------------------------------------------------------------------
-- Description :
--
--------------------------------------------------------------------------------

LIBRARY ieee;
USE ieee.std_logic_1164.all;

ENTITY mux_SSD IS
  PORT (
		digit1: in std_logic_vector(3 downto 0);
		digit2: in std_logic_vector(3 downto 0);
		digit3: in std_logic_vector(3 downto 0);
		digit4: in std_logic_vector(3 downto 0);
		sel1: in std_logic;
		sel2: in std_logic;
		rez: out std_logic_vector(3 downto 0)
    );
END mux_SSD;

ARCHITECTURE TypeArchitecture OF mux_SSD IS
signal aux:std_logic_vector(3 downto 0);
BEGIN
process(digit1,digit2,digit3,digit4,sel1,sel2)
begin
if sel1='0' and sel2='0'then aux<=digit1;
elsif sel1='1' and sel2='0' then aux<=digit2;
elsif sel1='0' and sel2='1' then aux<=digit3;
else aux<=digit4;
end if;
end process;
rez<=aux;
END TypeArchitecture;

// VHDL entity BCD_7_segmente, as the project stores it:
--------------------------------------------------------------------------------
-- Project :
-- File    :
-- Autor   :
-- Date    :
--
--------------------------------------------------------------------------------
-- Description :
--
--------------------------------------------------------------------------------

LIBRARY ieee;
USE ieee.std_logic_1164.all;

ENTITY BCD_7_segmente IS
  PORT (
	i:in std_logic_vector(3 downto 0);
  		o:out std_logic_vector(6 downto 0)
    );
END BCD_7_segmente;

--------------------------------------------------------------------------------
--Complete your VHDL description below
--------------------------------------------------------------------------------

ARCHITECTURE TypeArchitecture OF BCD_7_segmente IS

BEGIN
process(i)
begin
o<="0001110";
	if i=x"0" then o<="1111110";
	elsif i=x"1" then o<="0110000";
	elsif i=x"2" then o<="1101101";
	elsif i=x"3" then o<="1111001";
	elsif i=x"4" then o<="0110011";
	elsif i=x"5" then o<="1011011";
	elsif i=x"6" then o<="1011111";
	elsif i=x"7" then o<="1110000";
	elsif i=x"8" then o<="1111111";
	elsif i=x"9" then o<="1111011";
	elsif i=x"a" then o<="1110111";
	elsif i=x"b" then o<="0011111";
	elsif i=x"c" then o<="0001101";
	elsif i=x"d" then o<="0111101";
	elsif i=x"e" then o<="1101111";
	else o<="1000111";
end if;
end process;
END TypeArchitecture;
